// Logisim project A1_Grey.circ as structural Verilog: 1 circuit, main circuit main
module main (
  input  X,
  input  Y,
  output MSB,
  output LSB,
  output Unlocked
);

  wire _0_q, _0_qn, _1_q, _1_qn, _2_q, _2_qn, and_1_out, and_2_out, and_3_out, and_5_out, and_7_out,
       and_9_out, and_10_out, and_11_out, and_12_out, and_13_out, and_14_out, and_15_out, Enter_out,
       not_1_out, not_2_out, not_3_out, not_4_out, not_5_out, not_6_out, Reset_out, xor_1_out, xor_2_out,
       xor_3_out, xor_4_out, xor_5_out, xor_6_out, xor_7_out, xor_8_out, xor_9_out;

  Button Reset (.out(Reset_out));
  Button Enter (.out(Enter_out));
  xor xor_1 (xor_1_out, and_1_out, and_2_out);
  and and_1 (and_1_out, not_1_out, _2_qn, _1_qn, _0_q);
  not not_1 (not_1_out, Y);
  D_Flip_Flop _2 (.clk(Enter_out), .D(xor_1_out), .Q(_2_q), .Qn(_2_qn), .reset(Reset_out));  // open: preset, en
  and and_2 (and_2_out, not_2_out, _2_q, _1_qn, _0_q);
  not not_2 (not_2_out, Y);
  and and_3 (and_3_out, not_3_out, _2_qn, _1_q, _0_q);
  not not_3 (not_3_out, X);
  and and_4 (MSB, _2_qn, _1_q, _0_qn);
  xor xor_2 (xor_2_out, xor_3_out, and_7_out);
  xor xor_3 (xor_3_out, and_3_out, and_5_out);
  and and_5 (and_5_out, not_4_out, _2_q, _1_qn, _0_q);
  not not_4 (not_4_out, Y);
  and and_6 (LSB, _2_qn, _1_q, _0_q);
  D_Flip_Flop _1 (.clk(Enter_out), .D(xor_2_out), .Q(_1_q), .Qn(_1_qn), .reset(Reset_out));  // open: preset, en
  and and_7 (and_7_out, X, _2_q, _1_q, _0_q);
  and and_8 (Unlocked, _2_qn, _1_q, _0_qn);
  and and_9 (and_9_out, Y, _2_qn, _1_qn, _0_qn);
  xor xor_4 (xor_4_out, xor_5_out, xor_6_out);
  xor xor_5 (xor_5_out, and_9_out, and_10_out);
  and and_10 (and_10_out, not_5_out, _2_qn, _1_qn, _0_q);
  not not_5 (not_5_out, Y);
  xor xor_6 (xor_6_out, and_11_out, and_12_out);
  and and_11 (and_11_out, Y, _2_qn, _1_qn, _0_q);
  xor xor_7 (xor_7_out, xor_4_out, xor_9_out);
  and and_12 (and_12_out, not_6_out, _2_q, _1_qn, _0_q);
  not not_6 (not_6_out, Y);
  xor xor_8 (xor_8_out, and_13_out, and_15_out);
  and and_13 (and_13_out, Y, _2_q, _1_qn, _0_q);
  xor xor_9 (xor_9_out, xor_8_out, and_14_out);
  and and_14 (and_14_out, Y, _2_qn, _1_q, _0_qn);
  and and_15 (and_15_out, X, _2_q, _1_q, _0_q);
  D_Flip_Flop _0 (.clk(Enter_out), .D(xor_7_out), .Q(_0_q), .Qn(_0_qn), .reset(Reset_out));  // open: preset, en
endmodule
